# Fritzing sketch rc-drift-ble-cc2541-small (saved by Fritzing 0.8.5b)
circuit board: 2.39449cm x 1.62255cm
breadboards: 1

parts:
  M2 = DC Motor
  M3 = DC Motor
  CC1 = CC2541-small [part_number=cc2540]
  VCC1 = Battery
  J1 = female pin header, 4 pins [form="♀ (female)"]
  R5 = Resistor [tolerance=±5% resistance=4.7k package="0603 [SMD]"]
  C1 = Ceramic Capacitor [capacitance=100nF package="0603 [SMD, multilayer]"]
  C2 = Tantalum Capacitor [capacitance=1mF package="A 3216 [SMD, tantalum]"]
  LM11117 = Voltage Regulator LM1117 [package=sot223]
  10uF = Tantalum Capacitor [capacitance="1 μF" package="C 6032 [SMD, tantalum]"]
  10uF_2 = Tantalum Capacitor [capacitance="1 μF" package="C 6032 [SMD, tantalum]"]
  1 = lb1836m [chip_label=IC package=SOIC-14]
  R1 = Resistor [tolerance=±5% resistance=0 package="0603 [SMD]"]
  R3 = Resistor [tolerance=±5% resistance=4.7k package="0603 [SMD]"]
  R4 = Resistor [tolerance=±5% resistance=4.7k package="0603 [SMD]"]
  Q1 = NPN-Transistor [package="SOT-23 [SMD]"]
  Q2 = NPN-Transistor [package="SOT-23 [SMD]"]
  Q3 = NPN-Transistor [package="SOT-23 [SMD]"]
  Q4 = NPN-Transistor [package="SOT-23 [SMD]"]
  4_7k = Resistor [tolerance=±5% package="0402 [SMD]"]

nets:
  N1: M2.pin_1, 1.OUT1
  N2: M2.pin_2, 1.OUT2
  N3: M3.pin_1, 1.OUT3
  N4: M3.pin_2, 1.OUT4
  N5: CC1.3.3V, C1.0, C2.+, LM11117.OUT, 10uF.+, R1.Pin_0
  GND: CC1.GND, VCC1.-, C1.1, C2.-, LM11117.ADJ, 10uF.-, 10uF_2.-, 1.GND, Q1.2, Q2.2, Q3.2, Q4.2
  N6: CC1.P0.0, 4_7k.Pin_1
  N7: CC1.P0.1, R3.Pin_1
  N8: CC1.P0.2, R4.Pin_1
  N9: CC1.P0.3, 1.IN1
  N10: CC1.P0.4, 1.IN2
  N11: CC1.P0.5, 1.IN4
  N12: CC1.P0.6, 1.IN3
  N13: CC1.P0.7, R5.Pin_1
  N14: VCC1.+, LM11117.IN, 10uF_2.+, 1.VCC, 1.Vs1, 1.Vcont, 1.Vs2, R1.Pin_1
  N15: J1.pin1, Q1.1
  N16: J1.pin2, Q2.1
  N17: J1.pin3, Q3.1
  N18: J1.pin4, Q4.1
  N19: R5.Pin_0, Q4.0
  N20: R3.Pin_0, Q2.0
  N21: R4.Pin_0, Q3.0
  N22: Q1.0, 4_7k.Pin_0
