# Fritzing sketch rc-rec (saved by Fritzing 0.9.3b)
circuit board: 1.78681cm x 2.20776cm
breadboards: 1

parts:
  ESC_PWR = female pin header, 2 pins [form="♀ (female)"]
  BATT_IN = Battery block 9V
  R19 = Resistor [tolerance=±5% resistance=2.2k package="0603 [SMD]"]
  R18 = Resistor [tolerance=±5% resistance=2.2k package="0603 [SMD]"]
  C10 = Ceramic Capacitor [capacitance=100nF package="0603 [SMD, multilayer]"]
  C13 = Tantalum Capacitor [capacitance="1 μF" package="A 3216 [SMD, tantalum]"]
  C12 = Tantalum Capacitor [capacitance="1 μF" package="A 3216 [SMD, tantalum]"]
  Servo_+_ESC = double row female pin header, 6 pins [form="♀ (female)"]
  D2 = Rectifier Diode [package="Melf DO-213 AA [SMD]"]
  U4 = V_REG_MIC2920 [package=sot223]
  INA226 = INA226 [part_number=13 package=MSOP-10]
  R15 = Resistor [tolerance=±5% resistance=0.01 package="1206 [SMD]"]
  CC1 = CC2541-small [part_number=cc2540]
  Debug = female pin header, 9 pins [form="♀ (female)"]
  100Nf = Ceramic Capacitor [capacitance=100nF package="0603 [SMD, multilayer]"]
  0 = Resistor [tolerance=±5% resistance=220 package="0402 [SMD]"]
  10 = Resistor [tolerance=±5% resistance=10 package="0402 [SMD]"]
  0_2 = Resistor [tolerance=±5% resistance=220 package="0402 [SMD]"]
  10_2 = Resistor [tolerance=±5% resistance=10 package="0402 [SMD]"]
  15 = Resistor [tolerance=±5% resistance=15 package="0402 [SMD]"]

nets:
  N1: ESC_PWR.pin1, R15.Pin_1, 0.Pin_1, 10.Pin_0
  GND: ESC_PWR.pin2, BATT_IN.-, C10.0, C13.-, C12.-, Servo_+_ESC.pin3, Servo_+_ESC.pin4, U4.GND, INA226.A1, INA226.A0, INA226.GND, CC1.GND, Debug.pin9
  N2: BATT_IN.+, INA226.Vbus, R15.Pin_0, 10_2.Pin_0
  N3: R19.Pin_0, R18.Pin_0, C10.1, C12.+, U4.OUT, U4.OUT_PAD, CC1.3.3V, Debug.pin8
  N4: R19.Pin_1, INA226.SDA, CC1.SDA
  N5: R18.Pin_1, INA226.SCL, CC1.SCL
  N6: C13.+, D2.cathode, U4.IN
  N7: Servo_+_ESC.pin1, CC1.P0.7
  N8: Servo_+_ESC.pin2, Servo_+_ESC.pin5, 0_2.Pin_1
  N9: Servo_+_ESC.pin6, CC1.P0.6
  N10: D2.anode, 0.Pin_0, 0_2.Pin_0
  N11: INA226.Alert, CC1.P0.4
  N12: INA226.Vs+, 15.Pin_0
  N13: INA226.VIN-, 100Nf.0, 10.Pin_1
  N14: INA226.VIN+, 100Nf.1, 10_2.Pin_1
  N15: CC1.RESET, Debug.pin5
  N16: CC1.P2.1, Debug.pin6
  N17: CC1.P2.2, Debug.pin7
  N18: CC1.P0.0, Debug.pin2
  N19: CC1.P0.1, 15.Pin_1
  N20: CC1.P0.5, Debug.pin1
  N21: CC1.P1.6, Debug.pin3
  N22: CC1.P2.0, Debug.pin4

notes:
  -
  s
  t
  +
  power from esc or from battery

custom parts:
  V_REG_MIC2920: MIC2920A (http://www.micrel.com/_PDF/mic2920.pdf) - 400mA output LDO Regulator
  INA226: DESCRIPTION The INA226 is a current shunt and power monitor with an I2C interface. The INA226 monitors both a shunt voltage drop and bus supply voltage. Programmable calibration value, conversion times, and averaging, combined with an internal multiplier, enable direct readouts of current in amperes and power in watts.
