# Fritzing sketch rc-reventon-arduino (saved by Fritzing 0.8.3b)
circuit board: 2.69921cm x 2.00645cm
circuit board: 4.79991cm x 4.27853cm
breadboards: 1

parts:
  Order_No = H-Bridge [package=THT]
  Steering = DC Motor
  D1 = Rectifier Diode [part_number=1N4001 package="300 mil [THT]"]
  Arduino_Pro_mini = Arduino Pro Mini 3.3V
  +_- = Battery
  Throttle = DC Motor
  57836 = Bluetooth Chipset CSR [part_number=bc417143]
  R13 = Resistor [tolerance=±5% resistance=470 package=THT]
  R14 = Resistor [tolerance=±5% resistance=470 package=THT]
  R15 = Resistor [tolerance=±5% resistance=470 package=THT]
  R17 = Resistor [tolerance=±5% resistance=470 package=THT]
  Buzzer = Piezo Speaker
  J1 = female pin header, 3 pins [form="♀ (female)"]
  J5 = female pin header, 10 pins [form="♀ (female)"]
  Q1 = NPN-Transistor [package="TO92 [THT]"]
  R18 = Resistor [tolerance=±5% resistance=47 package=THT]
  LED1 = LED - 5mm [color="Infrared (940nm)" package="5 mm [THT]"]
  LED2 = LED - 5mm [color="Infrared (880nm)" package="5 mm [THT]"]
  LED3 = LED - 5mm [color="Red (633nm)" package="5 mm [THT]"]
  R21 = Resistor [tolerance=±5% resistance=470 package=THT]
  R22 = Resistor [tolerance=±5% resistance=470 package=THT]
  LED4 = LED - 5mm [color="Red (633nm)" package="5 mm [THT]"]
  LED5 = LED - 5mm [color="Red (633nm)" package="5 mm [THT]"]
  R23 = Resistor [tolerance=±5% resistance=470 package=THT]
  R24 = Resistor [tolerance=±5% resistance=470 package=THT]
  LED6 = LED - 5mm [color="Red (633nm)" package="5 mm [THT]"]
  LED7 = LED - 5mm [color="Red (633nm)" package="5 mm [THT]"]
  R25 = Resistor [tolerance=±5% resistance=220 package=THT]

nets:
  N1: Order_No.1_2EN, Arduino_Pro_mini.D7
  N2: Order_No.1A, Arduino_Pro_mini.D8
  N3: Order_No.1Y, Throttle.pin_1
  GND: Order_No.GND1, Order_No.GND2, Order_No.GND3, Order_No.GND4, Arduino_Pro_mini.GND, +_-.-, 57836.GRD, Buzzer.pin1, Q1.E, LED3.cathode, LED4.cathode, LED5.cathode, LED6.cathode, LED7.cathode
  N4: Order_No.2Y, Throttle.pin_2
  N5: Order_No.2A, Arduino_Pro_mini.MISO
  N6: Order_No.VCC2, D1.cathode
  N7: Order_No.3_4EN, Arduino_Pro_mini.D10, J5.pin10
  N8: Order_No.3A, Arduino_Pro_mini.MOSI, J5.pin9
  N9: Order_No.3Y, Steering.pin_2
  N10: Order_No.4Y, Steering.pin_1
  N11: Order_No.4A, Arduino_Pro_mini.D9
  N12: Order_No.VCC1, D1.anode, Arduino_Pro_mini.RAW, +_-.+
  N13: Arduino_Pro_mini.RESET, J5.pin1
  VCC: Arduino_Pro_mini.VCC, 57836.VCC, J5.pin2, R18.Pin_1
  N14: Arduino_Pro_mini.A3, J5.pin3, R23.Pin_0
  N15: Arduino_Pro_mini.A2, J5.pin4, R25.Pin_0
  N16: Arduino_Pro_mini.A1, J5.pin5, R21.Pin_1
  N17: Arduino_Pro_mini.A0, J5.pin6, R22.Pin_1
  N18: Arduino_Pro_mini.SCK, J5.pin7, R24.Pin_0
  N19: Arduino_Pro_mini.D6, R13.Pin_0
  N20: Arduino_Pro_mini.D5, R17.Pin_1
  N21: Arduino_Pro_mini.D4, 57836.TX
  N22: Arduino_Pro_mini.D3, R14.Pin_0, R15.Pin_0
  N23: Arduino_Pro_mini.D2, 57836.RX
  N24: R13.Pin_1, J1.pin1
  N25: R14.Pin_1, J1.pin2, Q1.B
  N26: R15.Pin_1, J1.pin3
  N27: R17.Pin_0, Buzzer.pin2
  N28: Q1.C, LED2.cathode
  N29: R18.Pin_0, LED1.anode
  N30: LED1.cathode, LED2.anode
  N31: LED3.anode, R25.Pin_1
  N32: R21.Pin_0, LED4.anode
  N33: R22.Pin_0, LED5.anode
  N34: R23.Pin_1, LED6.anode
  N35: R24.Pin_1, LED7.anode

notes:
  FL
  FR
  RL
  RR
  Stop
  IR LED

custom parts:
  Bluetooth Chipset CSR: Bluetooth module uses CSR Bluecore4
