# Fritzing sketch rc-simple (saved by Fritzing 0.9.3b)
circuit board: 2.39449cm x 1.62255cm
breadboards: 1

parts:
  Steering = DC Motor
  Throttle = DC Motor
  VCC1 = Battery
  Lights = female pin header, 4 pins [form="♀ (female)"]
  R5 = Resistor [tolerance=±5% resistance=4.7k package="0603 [SMD]"]
  C1 = Ceramic Capacitor [capacitance=100nF package="0603 [SMD, multilayer]"]
  C2 = Tantalum Capacitor [capacitance=1µF package="A 3216 [SMD, tantalum]"]
  LM11117 = Voltage Regulator LM1117 [package=sot223]
  10uF = Tantalum Capacitor [capacitance="1 μF" package="C 6032 [SMD, tantalum]"]
  10uF_2 = Tantalum Capacitor [capacitance="1 μF" package="C 6032 [SMD, tantalum]"]
  R1_-_DNC = Resistor [tolerance=±5% resistance=0 package="0603 [SMD]"]
  R3 = Resistor [tolerance=±5% resistance=4.7k package="0603 [SMD]"]
  R4 = Resistor [tolerance=±5% resistance=4.7k package="0603 [SMD]"]
  Q1 = NPN-Transistor [package="SOT-23 [SMD]"]
  Q2 = NPN-Transistor [package="SOT-23 [SMD]"]
  Q3 = NPN-Transistor [package="SOT-23 [SMD]"]
  Q4 = NPN-Transistor [package="SOT-23 [SMD]"]
  4_7k = Resistor [tolerance=±5% resistance=220 package="0402 [SMD]"]
  CC2542 = CC2541-small [part_number=cc2540]
  Part1 = lb1836m [chip_label=IC package=SOIC-14]

nets:
  N1: Steering.pin_1, Part1.OUT1
  N2: Steering.pin_2, Part1.OUT2
  N3: Throttle.pin_1, Part1.OUT3
  N4: Throttle.pin_2, Part1.OUT4
  GND: VCC1.-, C1.1, C2.-, LM11117.ADJ, 10uF.-, 10uF_2.-, Q1.2, Q2.2, Q3.2, Q4.2, CC2542.GND, Part1.GND
  5V: VCC1.+, LM11117.IN, 10uF_2.+, R1_-_DNC.Pin_1, Part1.VCC, Part1.Vs1, Part1.Vcont, Part1.Vs2
  N5: Lights.pin1, Q1.1
  N6: Lights.pin2, Q2.1
  N7: Lights.pin3, Q3.1
  N8: Lights.pin4, Q4.1
  N9: R5.Pin_0, Q4.0
  L4: R5.Pin_1, CC2542.P0.7
  3.3V: C1.0, C2.+, LM11117.OUT, 10uF.+, R1_-_DNC.Pin_0, CC2542.3.3V
  N10: R3.Pin_0, Q2.0
  L2: R3.Pin_1, CC2542.P0.1
  N11: R4.Pin_0, Q3.0
  L3: R4.Pin_1, CC2542.P0.2
  N12: Q1.0, 4_7k.Pin_0
  L1: 4_7k.Pin_1, CC2542.P0.0
  IN1: CC2542.P0.3, Part1.IN1
  IN2: CC2542.P0.4, Part1.IN2
  IN4: CC2542.P0.5, Part1.IN4
  IN3: CC2542.P0.6, Part1.IN3

notes:
  VCC + -
  SM
  TM
