# Fritzing sketch rc-wifi-esp8266 (saved by Fritzing 0.9.3b)
circuit board: 3.51821cm x 2.13268cm
breadboards: 1

parts:
  U1 = ESP8266-12 WiFi Module [part_number=ESP8266]
  0_1uF4 = Tantalum Capacitor [capacitance=100nF package="A 3216 [SMD, tantalum]"]
  J5 = female pin header, 2 pins [form="♀ (female)"]
  J6 = female pin header, 2 pins [form="♀ (female)"]
  J7 = female pin header, 2 pins [form="♀ (female)"]
  J8 = female pin header, 2 pins [form="♀ (female)"]
  0_1uF3 = Tantalum Capacitor [capacitance=100nF package="A 3216 [SMD, tantalum]"]
  R31 = Resistor [tolerance=±5% resistance=47k package="0603 [SMD]"]
  R32 = Resistor [tolerance=±5% resistance=47k package="0603 [SMD]"]
  R33 = Resistor [tolerance=±5% resistance=47k package="0603 [SMD]"]
  R36 = Resistor [tolerance=±5% resistance=220 package="0603 [SMD]"]
  R37 = Resistor [tolerance=±5% resistance=220 package="0603 [SMD]"]
  R34 = Resistor [tolerance=±5% resistance=220 package="0603 [SMD]"]
  R35 = Resistor [tolerance=±5% resistance=220 package="0603 [SMD]"]
  100nF = Ceramic Capacitor [capacitance=100nF package="0603 [SMD, multilayer]"]
  ESC = female pin header, 3 pins [form="♀ (female)"]
  Servo = female pin header, 3 pins [form="♀ (female)"]
  U4 = V_REG MIC5219 [package=sot23-5]
  470pF = Ceramic Capacitor [capacitance=100nF package="0603 [SMD, multilayer]"]
  U3 = Voltage Regulator LM1117 [package=sot223]
  ADC = female pin header, 1 pin [form="♀ (female)"]
  J10 = female pin header, 2 pins [form="♀ (female)"]
  R38 = Resistor [tolerance=±5% resistance=220 package="0603 [SMD]"]
  R39 = Resistor [tolerance=±5% resistance=0 package="0402 [SMD]"]
  R40 = Resistor [tolerance=±5% resistance=0 package="0402 [SMD]"]
  R41 = Resistor [tolerance=±5% resistance=0 package="0402 [SMD]"]
  Debug = female pin header, 4 pins [form="♀ (female)"]

nets:
  N1: U1.GPIO_0, R32.Pin_0, Debug.pin4
  N2: U1.GPIO_16, R36.Pin_0
  N3: U1.GPIO_1, R38.Pin_0
  N4: U1.CH_PD, R33.Pin_0
  GND: U1.GND, U1.GPIO_15, 0_1uF4.-, 0_1uF3.-, 100nF.1, ESC.pin3, Servo.pin3, U4.GND, 470pF.0, U3.ADJ, R41.Pin_0, Debug.pin3
  N5: U1.TXD, Debug.pin1
  N6: U1.ADC, ADC.pin1
  N7: U1.GPIO_14, R35.Pin_0
  N8: U1.GPIO_12, R34.Pin_0
  N9: U1.GPIO_13, R37.Pin_0
  N10: U1.GPIO_4, Servo.pin1
  N11: U1.GPIO_5, ESC.pin1
  N12: U1.RESET, R31.Pin_1
  N13: U1.RXD, Debug.pin2
  3.3V: U1.VCC, 0_1uF4.+, R31.Pin_0, R32.Pin_1, R33.Pin_1, 100nF.0, U4.OUT, U3.OUT, R40.Pin_0
  N14: J5.pin1, R34.Pin_1
  N15: J5.pin2, J6.pin2, J7.pin2, J8.pin2, J10.pin2, R39.Pin_1, R40.Pin_1, R41.Pin_1
  N16: J6.pin1, R35.Pin_1
  N17: J7.pin1, R36.Pin_1
  N18: J8.pin1, R37.Pin_1
  5V: 0_1uF3.+, ESC.pin2, Servo.pin2, U4.IN, U4.EN, U3.IN, R39.Pin_0
  N19: U4.BP, 470pF.1
  N20: J10.pin1, R38.Pin_1

notes:
  []
  S/T
  TX   RX  GND  GPIO0
  VCC
  GND
  3.3V
  Front Lights(GPIO16)
  Rear Lights (GPIO14)
  Left Turn Lights(GPIO12)
  Right Turn Lights(GPIO13)
  Reverse Lights(GPIO01)
  ADC
  only one LDO is needed
  0 Resistor selects leds drive, to GND, 3.3V or VCC

custom parts:
  ESP8266-12 WiFi Module: Generic WiFi Module based on the ESP8266 with onboard PCB antenna and UART communications
